# Fritzing sketch Final Circuit (saved by Fritzing 0.9.4)
breadboards: 1

parts:
  M4 = Dagu DGServo 9g (Top view) [part_number=RS001B]
  J1 = Basic Servo
  J2 = Basic Servo
  J3 = Basic Servo
  Power_plug1 = Power plug
  Part1 = Arduino Uno (Rev3)
  M2 = Dagu DGServo 9g (Top view) [part_number=RS001B]
  M3 = Dagu DGServo 9g (Top view) [part_number=RS001B]
  R1 = Resistor [tolerance=±5% resistance=220 package=THT]
  Part2 = Bluetooth HC-05 Macho  # not connected
  R2 = Resistor [tolerance=±5% resistance=220 package="1206 [SMD]"]

nets:
  GND: M4.gnd, J1.gnd, J2.gnd, J3.gnd, Power_plug1.GND, Part1.GND, M2.gnd, M3.gnd, R1.Pin_0
  VCC: M4.vcc, J1.vcc, J2.vcc, J3.vcc, Power_plug1.VCC, Part1.5V, M2.vcc, M3.vcc
  N1: M4.pulse, Part1.D9_PWM
  N2: J1.pulse, Part1.D8
  N3: J2.pulse, Part1.D6_PWM
  N4: J3.pulse, Part1.D7
  N5: Part1.D10_PWM/SS, M2.pulse
  N6: Part1.D4, R2.Pin_1
  N7: Part1.D5_PWM, M3.pulse
  N8: R1.Pin_1, R2.Pin_0

notes:
  2K
  1K
